# Fritzing sketch i2c (saved by Fritzing 0.7.12b)
breadboards: 1

parts:
  IC1 = 24LC256 [package=THT]
  R1 = Resistor [tolerance=±5% resistance=4.7k part_number=4k7 package=THT]
  R2 = Resistor [tolerance=±5% resistance=220 part_number=4k7 package=THT]
  IC2 = IC, DIP package, 10 pins [chip_label=MMA7660FC]

nets:
  N1: IC1.A0, IC1.0V, IC1.WP_-_Write_Protect, IC2.pin1, IC2.pin4, IC2.pin8, IC2.pin10
  N2: IC1.SDA_-_I2C_Data, R2.Pin_1, IC2.pin7
  N3: IC1.SCL_-_I2C_Clock, R1.Pin_1, IC2.pin6
  N4: IC1.+V, R1.Pin_0, R2.Pin_0, IC2.pin3, IC2.pin9
